// Logisim project guess_the_number.circ as structural Verilog: 11 circuits, main circuit main
module main (
  input  [3:0] in_1,
  input  Jogador,
  input  Jogar,
  input  [3:0] in_4,
  output Igual,
  output Maior,
  output Menor
);

  wire [2:0] Decodificador_2_out_6, Decodificador_out_6;
  wire [3:0] Decodificador_2_out_5, Decodificador_out_5, Multiplexador_out_4;

  Display Decodificador (
    .in_1(in_1[0]), .in_2(in_1[1]), .in_3(in_1[2]), .in_4(in_1[3]), .out_5(Decodificador_out_5),
    .out_6(Decodificador_out_6));
  Display Decodificador_2 (
    .in_1(in_4[0]), .in_2(in_4[1]), .in_3(in_4[2]), .in_4(in_4[3]), .out_5(Decodificador_2_out_5),
    .out_6(Decodificador_2_out_6));
  _7_Segment_Display u_7_segment_display_1 (
    .g(Decodificador_out_5[3]), .f(Decodificador_out_5[2]), .a(Decodificador_out_5[1]),
    .b(Decodificador_out_5[0]), .e(Decodificador_out_6[2]), .d(Decodificador_out_6[1]),
    .c(Decodificador_out_6[0]));  // open: dp
  Multiplexador Multiplexador (.in_1(in_1), .in_2(in_4), .in_3(Jogador), .out_4(Multiplexador_out_4));
  _7_Segment_Display u_7_segment_display_2 (
    .g(Decodificador_2_out_5[3]), .f(Decodificador_2_out_5[2]), .a(Decodificador_2_out_5[1]),
    .b(Decodificador_2_out_5[0]), .e(Decodificador_2_out_6[2]), .d(Decodificador_2_out_6[1]),
    .c(Decodificador_2_out_6[0]));  // open: dp
  Comparador comparador_1 (.in_1(Multiplexador_out_4), .in_2(Jogar), .I0___I1(Igual), .Maior(Maior), .Maior_2(Menor));
endmodule

module Comparador (
  input  [3:0] in_1,
  input  in_2,
  output I0___I1,
  output Maior,
  output Maior_2
);

  wire A0___B0_out, A1___B1_2_out, A1___B1_3_out, A1___B1_out, nor_1_out, not_1_out, not_2_out, not_3_out,
       not_4_out, or_1_out, xnor_1_out, xnor_2_out, xnor_3_out, xnor_4_out;

  xnor xnor_1 (xnor_1_out, in_1[3], 1'b0);
  xnor xnor_2 (xnor_2_out, in_1[2], 1'b1);
  xnor xnor_3 (xnor_3_out, in_1[1], 1'b1);
  xnor xnor_4 (xnor_4_out, in_1[0], 1'b0);
  not not_1 (not_1_out, 1'b0);
  not not_2 (not_2_out, 1'b1);
  not not_3 (not_3_out, 1'b1);
  not not_4 (not_4_out, 1'b0);
  and A0___B0 (A0___B0_out, in_1[3], not_1_out);
  and A1___B1 (A1___B1_out, in_1[2], not_2_out);
  and A1___B1_2 (A1___B1_2_out, in_1[1], not_3_out);
  and A1___B1_3 (A1___B1_3_out, xnor_1_out, xnor_2_out, xnor_3_out, in_1[0], not_4_out);
  and and_1 (I0___I1, xnor_4_out, xnor_3_out, xnor_2_out, xnor_1_out, in_2);
  or or_1 (or_1_out, A0___B0_out, A1___B1_out, A1___B1_2_out, A1___B1_3_out);
  and and_2 (Maior, or_1_out, in_2);
  nor nor_1 (nor_1_out, Maior, I0___I1);
  and and_3 (Maior_2, nor_1_out, in_2);
endmodule

// Disp - a
module a (
  input  in_1,
  input  in_2,
  input  in_3,
  input  in_4,
  output out_5
);

  wire and_1_out, and_2_out, not_1_out, not_2_out, not_3_out, not_4_out;

  and and_1 (and_1_out, in_2, in_4);
  not not_1 (not_1_out, in_1);
  not not_2 (not_2_out, in_2);
  and and_2 (and_2_out, not_1_out, not_2_out, not_3_out, not_4_out);
  not not_3 (not_3_out, in_3);
  not not_4 (not_4_out, in_4);
  or or_1 (out_5, in_1, in_3, and_1_out, and_2_out);
endmodule

// Disp - b
module b (
  input  in_1,
  input  in_2,
  input  in_3,
  input  in_4,
  output out_5
);

  wire and_1_out, and_2_out, and_3_out, and_4_out, and_5_out, not_1_out, not_2_out, not_3_out, not_4_out,
       not_5_out, not_6_out, not_7_out, not_8_out;

  not not_1 (not_1_out, in_1);
  not not_2 (not_2_out, in_2);
  not not_3 (not_3_out, in_2);
  not not_4 (not_4_out, in_1);
  not not_5 (not_5_out, in_3);
  not not_6 (not_6_out, in_4);
  not not_7 (not_7_out, in_1);
  not not_8 (not_8_out, in_3);
  and and_1 (and_1_out, not_1_out, not_2_out);
  and and_2 (and_2_out, in_1, not_3_out);
  and and_3 (and_3_out, not_4_out, in_2, not_5_out, not_6_out);
  and and_4 (and_4_out, not_7_out, in_2, in_3, in_4);
  and and_5 (and_5_out, in_1, in_2, not_8_out, in_4);
  or or_1 (out_5, and_1_out, and_2_out, and_3_out, and_4_out, and_5_out);
endmodule

// Disp - f
module f (
  input  in_1,
  input  in_2,
  input  in_3,
  input  in_4,
  output out_5
);

  wire and_1_out, and_2_out, and_3_out, not_1_out, not_2_out, not_3_out, not_4_out, not_5_out;

  not not_1 (not_1_out, in_3);
  not not_2 (not_2_out, in_3);
  not not_3 (not_3_out, in_4);
  not not_4 (not_4_out, in_1);
  not not_5 (not_5_out, in_4);
  and and_1 (and_1_out, in_2, not_1_out);
  and and_2 (and_2_out, not_2_out, not_3_out);
  and and_3 (and_3_out, not_4_out, in_2, in_3, not_5_out);
  or or_1 (out_5, in_1, and_1_out, and_2_out, and_3_out);
endmodule

// Disp - g
module g (
  input  in_1,
  input  in_2,
  input  in_3,
  input  in_4,
  output out_5
);

  wire and_1_out, and_2_out, and_3_out, and_4_out, not_1_out, not_2_out, not_3_out, xor_1_out;

  not not_1 (not_1_out, in_2);
  not not_2 (not_2_out, in_4);
  not not_3 (not_3_out, in_1);
  xor xor_1 (xor_1_out, in_2, in_3);
  and and_1 (and_1_out, in_1, not_1_out);
  and and_2 (and_2_out, in_3, not_2_out);
  and and_3 (and_3_out, in_1, in_3);
  and and_4 (and_4_out, not_3_out, xor_1_out);
  or or_1 (out_5, and_1_out, and_2_out, and_3_out, and_4_out);
endmodule

// Disp - e
module e (
  input  in_1,
  input  in_2,
  input  in_3,
  input  in_4,
  output out_5
);

  wire and_1_out, and_2_out, and_3_out, and_4_out, and_5_out, not_1_out, not_2_out, not_3_out, not_4_out,
       not_5_out, not_6_out, not_7_out;

  not not_1 (not_1_out, in_2);
  not not_2 (not_2_out, in_4);
  not not_3 (not_3_out, in_4);
  not not_4 (not_4_out, in_1);
  not not_5 (not_5_out, in_2);
  not not_6 (not_6_out, in_3);
  not not_7 (not_7_out, in_4);
  and and_1 (and_1_out, in_1, not_1_out, not_2_out);
  and and_2 (and_2_out, in_1, in_2);
  and and_3 (and_3_out, in_3, not_3_out);
  and and_4 (and_4_out, in_1, in_3);
  and and_5 (and_5_out, not_4_out, not_5_out, not_6_out, not_7_out);
  or or_1 (out_5, and_1_out, and_2_out, and_3_out, and_4_out, and_5_out);
endmodule

// Disp - d
module d (
  input  in_1,
  input  in_2,
  input  in_3,
  input  in_4,
  output out_5
);

  wire and_1_out, and_2_out, and_3_out, and_4_out, and_5_out, and_6_out, and_7_out, not_1_out, not_2_out,
       not_3_out, not_4_out, not_5_out, not_6_out, not_7_out, not_8_out, not_9_out, not_10_out, not_11_out,
       not_12_out, or_1_out;

  not not_1 (not_1_out, in_1);
  not not_2 (not_2_out, in_2);
  not not_3 (not_3_out, in_3);
  not not_4 (not_4_out, in_4);
  not not_5 (not_5_out, in_3);
  not not_6 (not_6_out, in_3);
  not not_7 (not_7_out, in_2);
  not not_8 (not_8_out, in_4);
  not not_9 (not_9_out, in_1);
  not not_10 (not_10_out, in_4);
  not not_11 (not_11_out, in_1);
  not not_12 (not_12_out, in_2);
  and and_1 (and_1_out, not_1_out, not_2_out, not_3_out, not_4_out);
  and and_2 (and_2_out, in_1, not_5_out);
  and and_3 (and_3_out, in_2, not_6_out, in_4);
  and and_4 (and_4_out, in_1, not_7_out, in_4);
  and and_5 (and_5_out, in_2, in_3, not_8_out);
  and and_6 (and_6_out, not_9_out, in_3, not_10_out);
  and and_7 (and_7_out, not_11_out, not_12_out, in_3);
  or or_1 (or_1_out, and_1_out, and_2_out, and_3_out, and_4_out, and_5_out);
  or or_2 (out_5, or_1_out, and_7_out, and_6_out);
endmodule

// Disp -c
module c (
  input  in_1,
  input  in_2,
  input  in_3,
  input  in_4,
  output out_5
);

  wire and_1_out, and_2_out, and_3_out, and_4_out, and_5_out, not_1_out, not_2_out, not_3_out, not_4_out,
       not_5_out, not_6_out;

  not not_1 (not_1_out, in_1);
  not not_2 (not_2_out, in_3);
  and and_1 (and_1_out, not_1_out, not_2_out);
  not not_3 (not_3_out, in_1);
  and and_2 (and_2_out, not_3_out, in_4);
  not not_4 (not_4_out, in_1);
  and and_3 (and_3_out, not_4_out, in_2, in_3);
  not not_5 (not_5_out, in_3);
  and and_4 (and_4_out, not_5_out, in_4);
  not not_6 (not_6_out, in_2);
  and and_5 (and_5_out, in_1, not_6_out);
  or or_1 (out_5, and_1_out, and_2_out, and_3_out, and_4_out, and_5_out);
endmodule

module Display (
  input  in_1,
  input  in_2,
  input  in_3,
  input  in_4,
  output [3:0] out_5,
  output [2:0] out_6
);

  a a_1 (.in_1(in_4), .in_2(in_3), .in_3(in_2), .in_4(in_1), .out_5(out_5[1]));
  b b_1 (.in_1(in_4), .in_2(in_3), .in_3(in_2), .in_4(in_1), .out_5(out_5[0]));
  c c_1 (.in_1(in_4), .in_2(in_3), .in_3(in_2), .in_4(in_1), .out_5(out_6[0]));
  d d_1 (.in_1(in_4), .in_2(in_3), .in_3(in_2), .in_4(in_1), .out_5(out_6[1]));
  e e_1 (.in_1(in_4), .in_2(in_3), .in_3(in_2), .in_4(in_1), .out_5(out_6[2]));
  f f_1 (.in_1(in_4), .in_2(in_3), .in_3(in_2), .in_4(in_1), .out_5(out_5[2]));
  g g_1 (.in_1(in_4), .in_2(in_3), .in_3(in_2), .in_4(in_1), .out_5(out_5[3]));
  _7_Segment_Display u_7_segment_display_1 (
    .g(out_5[3]), .f(out_5[2]), .a(out_5[1]), .b(out_5[0]), .e(out_6[2]), .d(out_6[1]), .c(out_6[0]));  // open: dp
endmodule

module Multiplexador (
  input  [3:0] in_1,
  input  [3:0] in_2,
  input  in_3,
  output [3:0] out_4
);

  wire and_1_out, and_2_out, and_3_out, and_4_out, and_5_out, and_6_out, and_7_out, and_8_out, not_1_out,
       not_2_out, not_3_out, not_4_out;

  and and_1 (and_1_out, in_1[0], not_1_out);
  not not_1 (not_1_out, in_3);
  and and_2 (and_2_out, in_2[0], in_3);
  and and_3 (and_3_out, in_1[1], not_2_out);
  not not_2 (not_2_out, in_3);
  and and_4 (and_4_out, in_2[1], in_3);
  and and_5 (and_5_out, in_1[2], not_3_out);
  not not_3 (not_3_out, in_3);
  and and_6 (and_6_out, in_2[2], in_3);
  and and_7 (and_7_out, in_1[3], not_4_out);
  not not_4 (not_4_out, in_3);
  and and_8 (and_8_out, in_2[3], in_3);
  or or_1 (out_4[0], and_1_out, and_2_out);
  or or_2 (out_4[1], and_3_out, and_4_out);
  or or_3 (out_4[2], and_5_out, and_6_out);
  or or_4 (out_4[3], and_7_out, and_8_out);
endmodule
